// Logisim project 4_bit_fisherman.circ as structural Verilog: 21 circuits, main circuit half_adder
module half_adder (
  input  A,
  input  B,
  output SUM,
  output Cout
);

  xor xor_1 (SUM, A, B);
  and and_1 (Cout, A, B);
endmodule

module full_adder (
  input  A,
  input  B,
  input  Cin,
  output Sum,
  output Cout
);

  wire and_1_out, and_2_out, xor_1_out;

  xor xor_1 (xor_1_out, A, B);
  and and_1 (and_1_out, A, B);
  xor xor_2 (Sum, xor_1_out, Cin);
  and and_2 (and_2_out, xor_1_out, Cin);
  or or_1 (Cout, and_2_out, and_1_out);
endmodule

module d_latch (
  input  E,
  input  D,
  output Q,
  output Qc
);

  wire and_1_out, and_2_out, not_1_out;

  not not_1 (not_1_out, D);
  and and_1 (and_1_out, not_1_out, E);
  and and_2 (and_2_out, E, D);
  nor nor_1 (Q, and_1_out, Qc);
  nor nor_2 (Qc, Q, and_2_out);
endmodule

module ALU (
  input  [3:0] A,
  input  [3:0] B,
  input  Subtract_mode,
  output [3:0] Sum,
  output Overflow
);

  wire ripple_carry_adder_1_c3, ripple_carry_adder_1_cout;
  wire [3:0] xor_1_out;

  xor xor_1 (xor_1_out[0], B[0], Subtract_mode);
  xor xor_2 (xor_1_out[1], B[1], Subtract_mode);
  xor xor_3 (xor_1_out[2], B[2], Subtract_mode);
  xor xor_4 (xor_1_out[3], B[3], Subtract_mode);
  ripple_carry_adder ripple_carry_adder_1 (
    .Cin0(Subtract_mode), .A(A), .B(xor_1_out), .Result(Sum), .Cout(ripple_carry_adder_1_cout),
    .C3(ripple_carry_adder_1_c3));
  xor xor_5 (Overflow, ripple_carry_adder_1_cout, ripple_carry_adder_1_c3);
endmodule

module ripple_carry_adder (
  input  Cin0,
  input  [3:0] A,
  input  [3:0] B,
  output [3:0] Result,
  output Cout,
  output C3
);

  wire full_adder_1_cout, full_adder_2_cout;

  full_adder full_adder_1 (.A(A[0]), .B(B[0]), .Cin(Cin0), .Sum(Result[0]), .Cout(full_adder_1_cout));
  full_adder full_adder_2 (.A(A[1]), .B(B[1]), .Cin(full_adder_1_cout), .Sum(Result[1]), .Cout(full_adder_2_cout));
  full_adder full_adder_3 (.A(A[2]), .B(B[2]), .Cin(full_adder_2_cout), .Sum(Result[2]), .Cout(C3));
  full_adder full_adder_4 (.A(A[3]), .B(B[3]), .Cin(C3), .Sum(Result[3]), .Cout(Cout));
endmodule

module main (
  input  sub,
  input  mult,
  input  [3:0] A,
  input  CLK,
  input  [3:0] B,
  input  WE,
  input  OE
);

  wire cpu_1_over_flag, nand_1_out, xor_1_out, xor_2_out;
  wire [3:0] four_bit_memory_1_out_4, sm_mem;
  wire [6:0] decoder_7segment_4bit_1_out_2, decoder_7segment_4bit_2_out_2, decoder_7segment_4bit_3_out_2,
       decoder_7segment_4bit_4_out_2;

  decoder_7segment_4bit decoder_7segment_4bit_1 (.in_1(A), .out_2(decoder_7segment_4bit_1_out_2));
  decoder_7segment_4bit decoder_7segment_4bit_2 (.in_1(B), .out_2(decoder_7segment_4bit_2_out_2));
  LED led_1 (.in(decoder_7segment_4bit_1_out_2[5]));
  LED led_2 (.in(decoder_7segment_4bit_1_out_2[5]));
  LED led_3 (.in(decoder_7segment_4bit_1_out_2[5]));
  LED led_4 (.in(decoder_7segment_4bit_1_out_2[4]));
  LED led_5 (.in(decoder_7segment_4bit_1_out_2[4]));
  LED led_6 (.in(decoder_7segment_4bit_1_out_2[4]));
  LED led_7 (.in(decoder_7segment_4bit_1_out_2[0]));
  LED led_8 (.in(decoder_7segment_4bit_1_out_2[0]));
  LED led_9 (.in(decoder_7segment_4bit_1_out_2[0]));
  LED led_10 (.in(decoder_7segment_4bit_1_out_2[1]));
  LED led_11 (.in(decoder_7segment_4bit_1_out_2[1]));
  LED led_12 (.in(decoder_7segment_4bit_1_out_2[1]));
  LED led_13 (.in(decoder_7segment_4bit_1_out_2[6]));
  LED led_14 (.in(decoder_7segment_4bit_1_out_2[6]));
  LED led_15 (.in(decoder_7segment_4bit_1_out_2[6]));
  LED led_16 (.in(decoder_7segment_4bit_1_out_2[2]));
  LED led_17 (.in(decoder_7segment_4bit_1_out_2[2]));
  LED led_18 (.in(decoder_7segment_4bit_1_out_2[2]));
  LED led_19 (.in(decoder_7segment_4bit_1_out_2[3]));
  LED led_20 (.in(decoder_7segment_4bit_1_out_2[3]));
  LED led_21 (.in(decoder_7segment_4bit_1_out_2[3]));
  LED led_22 (.in(A[3]));
  LED led_23 (.in(A[3]));
  LED led_24 (.in(A[3]));
  LED led_25 (.in(mult));
  LED led_26 (.in(mult));
  LED led_27 (.in(mult));
  LED led_28 (.in(mult));
  LED led_29 (.in(mult));
  LED led_30 (.in(mult));
  LED led_31 (.in(mult));
  LED led_32 (.in(mult));
  LED led_33 (.in(mult));
  LED led_34 (.in(xor_1_out));
  LED led_35 (.in(xor_1_out));
  LED led_36 (.in(xor_2_out));
  LED led_37 (.in(xor_2_out));
  LED led_38 (.in(xor_2_out));
  LED led_39 (.in(xor_1_out));
  LED led_40 (.in(xor_1_out));
  four_bit_memory four_bit_memory_1 (.WE(WE), .D(sm_mem), .OE(OE), .out_4(four_bit_memory_1_out_4));
  decoder_7segment_4bit decoder_7segment_4bit_3 (.in_1(four_bit_memory_1_out_4), .out_2(decoder_7segment_4bit_3_out_2));
  LED led_41 (.in(mult));
  LED led_42 (.in(mult));
  LED led_43 (.in(mult));
  LED led_44 (.in(mult));
  xor xor_1 (xor_1_out, mult, nand_1_out);
  LED led_45 (.in(xor_2_out));
  LED led_46 (.in(xor_2_out));
  xor xor_2 (xor_2_out, 1'b1, mult);
  CPU cpu_1 (
    .Data_in_A(A), .Data_in_B(B), .enA(CLK), .enB(CLK), .cloc(CLK), .Subtract_mode(sub), .mult(mult),
    .res(sm_mem), .over_flag(cpu_1_over_flag));
  LED led_47 (.in(decoder_7segment_4bit_2_out_2[0]));
  LED led_48 (.in(decoder_7segment_4bit_2_out_2[0]));
  LED led_49 (.in(decoder_7segment_4bit_2_out_2[0]));
  LED led_50 (.in(decoder_7segment_4bit_2_out_2[5]));
  LED led_51 (.in(decoder_7segment_4bit_2_out_2[5]));
  LED led_52 (.in(decoder_7segment_4bit_2_out_2[5]));
  LED led_53 (.in(decoder_7segment_4bit_2_out_2[6]));
  LED led_54 (.in(decoder_7segment_4bit_2_out_2[6]));
  LED led_55 (.in(decoder_7segment_4bit_2_out_2[6]));
  LED led_56 (.in(decoder_7segment_4bit_2_out_2[4]));
  LED led_57 (.in(decoder_7segment_4bit_2_out_2[4]));
  LED led_58 (.in(decoder_7segment_4bit_2_out_2[4]));
  LED led_59 (.in(decoder_7segment_4bit_2_out_2[3]));
  LED led_60 (.in(decoder_7segment_4bit_2_out_2[3]));
  LED led_61 (.in(decoder_7segment_4bit_2_out_2[3]));
  nand nand_1 (nand_1_out, xor_2_out, sub);
  LED led_62 (.in(B[3]));
  LED led_63 (.in(B[3]));
  LED led_64 (.in(four_bit_memory_1_out_4[3]));
  LED led_65 (.in(four_bit_memory_1_out_4[3]));
  LED led_66 (.in(four_bit_memory_1_out_4[3]));
  LED led_67 (.in(cpu_1_over_flag));
  LED led_68 (.in(cpu_1_over_flag));
  LED led_69 (.in(cpu_1_over_flag));
  LED led_70 (.in(cpu_1_over_flag));
  LED led_71 (.in(cpu_1_over_flag));
  LED led_72 (.in(cpu_1_over_flag));
  LED led_73 (.in(cpu_1_over_flag));
  LED led_74 (.in(decoder_7segment_4bit_2_out_2[1]));
  LED led_75 (.in(decoder_7segment_4bit_2_out_2[1]));
  LED led_76 (.in(decoder_7segment_4bit_2_out_2[1]));
  LED led_77 (.in(1'b1));
  LED led_78 (.in(decoder_7segment_4bit_2_out_2[2]));
  LED led_79 (.in(1'b1));
  LED led_80 (.in(decoder_7segment_4bit_2_out_2[2]));
  LED led_81 (.in(decoder_7segment_4bit_2_out_2[2]));
  LED led_82 (.in(B[3]));
  LED led_83 (.in(decoder_7segment_4bit_3_out_2[0]));
  LED led_84 (.in(decoder_7segment_4bit_3_out_2[0]));
  LED led_85 (.in(decoder_7segment_4bit_3_out_2[5]));
  LED led_86 (.in(decoder_7segment_4bit_3_out_2[5]));
  LED led_87 (.in(decoder_7segment_4bit_3_out_2[5]));
  LED led_88 (.in(decoder_7segment_4bit_3_out_2[6]));
  LED led_89 (.in(decoder_7segment_4bit_3_out_2[6]));
  LED led_90 (.in(decoder_7segment_4bit_3_out_2[4]));
  LED led_91 (.in(decoder_7segment_4bit_3_out_2[4]));
  LED led_92 (.in(decoder_7segment_4bit_3_out_2[4]));
  LED led_93 (.in(decoder_7segment_4bit_3_out_2[3]));
  LED led_94 (.in(decoder_7segment_4bit_3_out_2[3]));
  LED led_95 (.in(cpu_1_over_flag));
  LED led_96 (.in(cpu_1_over_flag));
  LED led_97 (.in(cpu_1_over_flag));
  LED led_98 (.in(cpu_1_over_flag));
  LED led_99 (.in(cpu_1_over_flag));
  LED led_100 (.in(cpu_1_over_flag));
  LED led_101 (.in(cpu_1_over_flag));
  LED led_102 (.in(cpu_1_over_flag));
  LED led_103 (.in(cpu_1_over_flag));
  LED led_104 (.in(cpu_1_over_flag));
  LED led_105 (.in(cpu_1_over_flag));
  LED led_106 (.in(cpu_1_over_flag));
  LED led_107 (.in(1'b1));
  LED led_108 (.in(1'b1));
  LED led_109 (.in(1'b1));
  LED led_110 (.in(1'b1));
  LED led_111 (.in(1'b1));
  LED led_112 (.in(1'b1));
  LED led_113 (.in(decoder_7segment_4bit_3_out_2[0]));
  LED led_114 (.in(decoder_7segment_4bit_3_out_2[1]));
  LED led_115 (.in(decoder_7segment_4bit_3_out_2[1]));
  LED led_116 (.in(decoder_7segment_4bit_3_out_2[1]));
  LED led_117 (.in(decoder_7segment_4bit_3_out_2[6]));
  LED led_118 (.in(decoder_7segment_4bit_3_out_2[2]));
  LED led_119 (.in(decoder_7segment_4bit_3_out_2[2]));
  LED led_120 (.in(decoder_7segment_4bit_3_out_2[2]));
  LED led_121 (.in(decoder_7segment_4bit_3_out_2[3]));
  LED led_122 (.in(sm_mem[3]));
  LED led_123 (.in(sm_mem[3]));
  LED led_124 (.in(sm_mem[3]));
  decoder_7segment_4bit decoder_7segment_4bit_4 (.in_1(sm_mem), .out_2(decoder_7segment_4bit_4_out_2));
  LED led_125 (.in(decoder_7segment_4bit_4_out_2[0]));
  LED led_126 (.in(decoder_7segment_4bit_4_out_2[0]));
  LED led_127 (.in(decoder_7segment_4bit_4_out_2[5]));
  LED led_128 (.in(decoder_7segment_4bit_4_out_2[5]));
  LED led_129 (.in(decoder_7segment_4bit_4_out_2[5]));
  LED led_130 (.in(decoder_7segment_4bit_4_out_2[6]));
  LED led_131 (.in(decoder_7segment_4bit_4_out_2[6]));
  LED led_132 (.in(decoder_7segment_4bit_4_out_2[4]));
  LED led_133 (.in(decoder_7segment_4bit_4_out_2[4]));
  LED led_134 (.in(decoder_7segment_4bit_4_out_2[4]));
  LED led_135 (.in(decoder_7segment_4bit_4_out_2[3]));
  LED led_136 (.in(decoder_7segment_4bit_4_out_2[3]));
  LED led_137 (.in(decoder_7segment_4bit_4_out_2[0]));
  LED led_138 (.in(decoder_7segment_4bit_4_out_2[1]));
  LED led_139 (.in(decoder_7segment_4bit_4_out_2[1]));
  LED led_140 (.in(decoder_7segment_4bit_4_out_2[1]));
  LED led_141 (.in(decoder_7segment_4bit_4_out_2[6]));
  LED led_142 (.in(decoder_7segment_4bit_4_out_2[2]));
  LED led_143 (.in(decoder_7segment_4bit_4_out_2[2]));
  LED led_144 (.in(decoder_7segment_4bit_4_out_2[2]));
  LED led_145 (.in(decoder_7segment_4bit_4_out_2[3]));

  // Other names for the same wires on the sheet: m = mult

  // Notes on the sheet:
  //   MEMORY
  //   Ini tanda minus
  //   Jika input masih 0-0 tapi udah ada hasil, itu hasil dari 
  //   angka yang ada dalam register, yang tidak ditampilin
  //   pada seven segment, aktifkan clock untuk memperbaiki
  //   Activate Clock to get results
  //   Ini tanda minus
endmodule

module decoder_7segment_4bit (
  input  [3:0] in_1,
  output [6:0] out_2
);

  wire nor_1_out, seven_0_1_out_2, seven_1_1_out_2, seven_2_1_out_2, seven_3_1_out_2, seven_4_1_out_2,
       seven_5_1_out_2;

  seven_0 seven_0_1 (.in_1(in_1), .out_2(seven_0_1_out_2));
  seven_1 seven_1_1 (.in_1(in_1), .out_2(seven_1_1_out_2));
  seven_2 seven_2_1 (.in_1(in_1), .out_2(seven_2_1_out_2));
  seven_3 seven_3_1 (.in_1(in_1), .out_2(seven_3_1_out_2));
  seven_4 seven_4_1 (.in_1(in_1), .out_2(seven_4_1_out_2));
  seven_5 seven_5_1 (.in_1(in_1), .out_2(seven_5_1_out_2));
  seven_6 seven_6_1 (.in_1(in_1), .out_2(out_2[6]));
  nor nor_1 (nor_1_out, out_2[6], seven_5_1_out_2, seven_4_1_out_2, seven_3_1_out_2, seven_2_1_out_2, seven_1_1_out_2, seven_0_1_out_2);
  or or_1 (out_2[0], seven_0_1_out_2, nor_1_out);
  or or_2 (out_2[1], seven_1_1_out_2, nor_1_out);
  or or_3 (out_2[2], seven_2_1_out_2, nor_1_out);
  or or_4 (out_2[3], seven_3_1_out_2, nor_1_out);
  or or_5 (out_2[4], nor_1_out, seven_4_1_out_2);
  or or_6 (out_2[5], seven_5_1_out_2, nor_1_out);
endmodule

module seven_0 (
  input  [3:0] in_1,
  output out_2
);

  wire and_1_out, and_2_out, and_3_out, and_4_out, not_1_out, not_2_out, not_3_out, not_4_out;

  not not_1 (not_1_out, in_1[2]);
  not not_2 (not_2_out, in_1[0]);
  not not_3 (not_3_out, in_1[3]);
  not not_4 (not_4_out, in_1[1]);
  and and_1 (and_1_out, in_1[3], not_1_out);
  and and_2 (and_2_out, in_1[1], not_2_out);
  and and_3 (and_3_out, in_1[1], not_3_out);
  and and_4 (and_4_out, in_1[2], not_4_out, in_1[0]);
  or or_1 (out_2, and_1_out, and_2_out, and_3_out, and_4_out);
endmodule

module seven_1 (
  input  [3:0] in_1,
  output out_2
);

  wire and_1_out, and_2_out, and_3_out, and_4_out, and_5_out, and_6_out, not_1_out, not_2_out, not_3_out,
       not_4_out, not_5_out, not_6_out, not_7_out, not_8_out;

  not not_1 (not_1_out, in_1[1]);
  not not_2 (not_2_out, in_1[0]);
  not not_3 (not_3_out, in_1[1]);
  not not_4 (not_4_out, in_1[2]);
  not not_5 (not_5_out, in_1[3]);
  not not_6 (not_6_out, in_1[3]);
  not not_7 (not_7_out, in_1[2]);
  not not_8 (not_8_out, in_1[3]);
  and and_1 (and_1_out, in_1[3], in_1[2]);
  and and_2 (and_2_out, in_1[3], not_1_out);
  and and_3 (and_3_out, in_1[2], not_2_out, not_3_out);
  and and_4 (and_4_out, in_1[1], not_4_out, not_5_out);
  and and_5 (and_5_out, not_6_out, in_1[1], in_1[0]);
  and and_6 (and_6_out, in_1[0], not_7_out, not_8_out);
  or or_1 (out_2, and_1_out, and_2_out, and_3_out, and_4_out, and_5_out, and_6_out);
endmodule

module seven_3 (
  input  [3:0] in_1,
  output out_2
);

  wire and_1_out, and_2_out, and_3_out, and_4_out, not_1_out, not_2_out, not_3_out, not_4_out, not_5_out;

  not not_1 (not_1_out, in_1[0]);
  not not_2 (not_2_out, in_1[2]);
  not not_3 (not_3_out, in_1[2]);
  not not_4 (not_4_out, in_1[0]);
  not not_5 (not_5_out, in_1[1]);
  and and_1 (and_1_out, in_1[1], not_1_out);
  and and_2 (and_2_out, in_1[1], not_2_out);
  and and_3 (and_3_out, in_1[3], not_3_out, not_4_out);
  and and_4 (and_4_out, in_1[2], not_5_out, in_1[0]);
  or or_1 (out_2, and_1_out, and_2_out, and_3_out, and_4_out);
endmodule

module seven_2 (
  input  [3:0] in_1,
  output out_2
);

  wire and_1_out, and_2_out, and_3_out, not_1_out, not_2_out, not_3_out;

  not not_1 (not_1_out, in_1[3]);
  not not_2 (not_2_out, in_1[2]);
  not not_3 (not_3_out, in_1[1]);
  and and_1 (and_1_out, in_1[2], not_1_out);
  and and_2 (and_2_out, in_1[3], not_2_out);
  and and_3 (and_3_out, in_1[3], not_3_out);
  or or_1 (out_2, in_1[0], and_1_out, and_2_out, and_3_out);
endmodule

module seven_4 (
  input  [3:0] in_1,
  output out_2
);

  wire and_1_out, and_2_out, not_1_out, not_2_out, not_3_out;

  not not_1 (not_1_out, in_1[0]);
  not not_2 (not_2_out, in_1[2]);
  not not_3 (not_3_out, in_1[0]);
  and and_1 (and_1_out, in_1[1], not_1_out);
  and and_2 (and_2_out, in_1[3], not_2_out, not_3_out);
  or or_1 (out_2, and_1_out, and_2_out);
endmodule

module seven_5 (
  input  [3:0] in_1,
  output out_2
);

  wire and_1_out, and_2_out, and_3_out, and_4_out, not_1_out, not_2_out, not_3_out, not_4_out, not_5_out,
       not_6_out, not_7_out;

  not not_1 (not_1_out, in_1[3]);
  not not_2 (not_2_out, in_1[1]);
  not not_3 (not_3_out, in_1[1]);
  not not_4 (not_4_out, in_1[0]);
  not not_5 (not_5_out, in_1[2]);
  not not_6 (not_6_out, in_1[3]);
  not not_7 (not_7_out, in_1[0]);
  and and_1 (and_1_out, in_1[2], not_1_out, not_2_out);
  and and_2 (and_2_out, in_1[3], not_3_out, not_4_out);
  and and_3 (and_3_out, in_1[3], not_5_out, in_1[1]);
  and and_4 (and_4_out, in_1[2], not_6_out, not_7_out);
  or or_1 (out_2, and_1_out, and_2_out, and_3_out, and_4_out);
endmodule

module seven_6 (
  input  [3:0] in_1,
  output out_2
);

  wire and_1_out, and_2_out, and_3_out, and_4_out, not_1_out, not_2_out, not_3_out, not_4_out;

  not not_1 (not_1_out, in_1[2]);
  not not_2 (not_2_out, in_1[0]);
  not not_3 (not_3_out, in_1[1]);
  not not_4 (not_4_out, in_1[0]);
  and and_1 (and_1_out, in_1[1], not_1_out);
  and and_2 (and_2_out, in_1[3], not_2_out);
  and and_3 (and_3_out, in_1[2], not_3_out);
  and and_4 (and_4_out, in_1[2], not_4_out);
  or or_1 (out_2, and_1_out, and_2_out, and_3_out, and_4_out);
endmodule

module four_bit_memory (
  input  WE,
  input  [3:0] D,
  input  OE,
  output [3:0] out_4
);

  wire d_latch_1_q, d_latch_2_q, d_latch_3_q, d_latch_4_q;

  d_latch d_latch_1 (.D(D[0]), .E(WE), .Q(d_latch_1_q));  // open: Qc
  d_latch d_latch_2 (.D(D[1]), .E(WE), .Q(d_latch_2_q));  // open: Qc
  d_latch d_latch_3 (.D(D[2]), .E(WE), .Q(d_latch_3_q));  // open: Qc
  d_latch d_latch_4 (.D(D[3]), .E(WE), .Q(d_latch_4_q));  // open: Qc
  and and_1 (out_4[0], d_latch_1_q, OE);
  and and_2 (out_4[1], d_latch_2_q, OE);
  and and_3 (out_4[2], d_latch_3_q, OE);
  and and_4 (out_4[3], d_latch_4_q, OE);
endmodule

module d_flip_flop (
  input  D,
  input  CLK,
  output Q,
  output Qc
);

  wire nand_1_out, nand_2_out, not_1_out;

  not not_1 (not_1_out, D);
  nand nand_1 (nand_1_out, D, CLK);
  nand nand_2 (nand_2_out, not_1_out, CLK);
  nand nand_3 (Q, nand_1_out, Qc);
  nand nand_4 (Qc, Q, nand_2_out);
endmodule

module CPU (
  input  [3:0] Data_in_A,
  input  enA,
  input  mult,
  input  [3:0] Data_in_B,
  input  enB,
  input  Subtract_mode,
  input  cloc,
  output [3:0] res,
  output over_flag
);

  wire [3:0] A, alu_1_sum, array_multiplier_1_res, B;

  four_bit_register four_bit_register_1 (.D(Data_in_A), .Enable(enA), .cloc(cloc), .Q(A));
  four_bit_register four_bit_register_2 (.D(Data_in_B), .Enable(enB), .cloc(cloc), .Q(B));
  ALU alu_1 (.A(A), .B(B), .Subtract_mode(Subtract_mode), .Sum(alu_1_sum), .Overflow(over_flag));
  mux_2_1 mux_2_1_1 (.S(mult), .in0(alu_1_sum[3]), .in1(array_multiplier_1_res[3]), .res(res[3]));
  array_multiplier array_multiplier_1 (.A(A), .B(B), .res(array_multiplier_1_res));
  mux_2_1 mux_2_1_2 (.S(mult), .in0(alu_1_sum[2]), .in1(array_multiplier_1_res[2]), .res(res[2]));
  mux_2_1 mux_2_1_3 (.S(mult), .in0(alu_1_sum[1]), .in1(array_multiplier_1_res[1]), .res(res[1]));
  mux_2_1 mux_2_1_4 (.S(mult), .in0(alu_1_sum[0]), .in1(array_multiplier_1_res[0]), .res(res[0]));
endmodule

module four_bit_register (
  input  [3:0] D,
  input  Enable,
  input  cloc,
  output [3:0] Q
);

  wire mux_2_1_1_res, mux_2_1_2_res, mux_2_1_3_res, mux_2_1_4_res, not_1_out;

  mux_2_1 mux_2_1_1 (.S(not_1_out), .in0(D[1]), .in1(Q[1]), .res(mux_2_1_1_res));
  mux_2_1 mux_2_1_2 (.S(not_1_out), .in0(D[2]), .in1(Q[2]), .res(mux_2_1_2_res));
  mux_2_1 mux_2_1_3 (.S(not_1_out), .in0(D[3]), .in1(Q[3]), .res(mux_2_1_3_res));
  not not_1 (not_1_out, Enable);
  mux_2_1 mux_2_1_4 (.S(not_1_out), .in0(D[0]), .in1(Q[0]), .res(mux_2_1_4_res));
  d_flip_flop d_flip_flop_1 (.D(mux_2_1_4_res), .CLK(cloc), .Q(Q[0]));  // open: Qc
  d_flip_flop d_flip_flop_2 (.D(mux_2_1_1_res), .CLK(cloc), .Q(Q[1]));  // open: Qc
  d_flip_flop d_flip_flop_3 (.D(mux_2_1_2_res), .CLK(cloc), .Q(Q[2]));  // open: Qc
  d_flip_flop d_flip_flop_4 (.D(mux_2_1_3_res), .CLK(cloc), .Q(Q[3]));  // open: Qc
endmodule

module mux_2_1 (
  input  in0,
  input  in1,
  input  S,
  output res
);

  wire and_1_out, and_2_out, not_1_out;

  not not_1 (not_1_out, S);
  and and_1 (and_1_out, in0, not_1_out);
  and and_2 (and_2_out, in1, S);
  or or_1 (res, and_1_out, and_2_out);
endmodule

module array_multiplier (
  input  [3:0] A,
  input  [3:0] B,
  output [3:0] res
);

  wire and_2_out, and_3_out, and_4_out, and_7_out, and_8_out, and_9_out, and_10_out, and_11_out, and_12_out,
       and_13_out, and_14_out, and_16_out, half_adder_1_cout, half_adder_1_sum, half_adder_3_cout,
       half_adder_4_cout, yet_another_full_adder_2_cout, yet_another_full_adder_3_cout,
       yet_another_full_adder_3_sum, yet_another_full_adder_4_cout, yet_another_full_adder_4_sum,
       yet_another_full_adder_5_cout, yet_another_full_adder_5_sum;

  yet_another_full_adder yet_another_full_adder_1 (
    .A(half_adder_1_cout), .B(and_3_out), .Cin(yet_another_full_adder_2_cout));  // open: Sum, Cout
  // AND_Gate and_1 has open pins: in0=B[3], in1=A[3], out=open
  and and_2 (and_2_out, B[1], A[3]);
  half_adder half_adder_1 (
    .A(and_2_out), .B(yet_another_full_adder_3_cout), .Cout(half_adder_1_cout), .SUM(half_adder_1_sum));
  and and_3 (and_3_out, B[2], A[3]);
  and and_4 (and_4_out, B[2], A[2]);
  yet_another_full_adder yet_another_full_adder_2 (
    .A(half_adder_1_sum), .B(and_4_out), .Cin(yet_another_full_adder_5_cout),
    .Cout(yet_another_full_adder_2_cout));  // open: Sum
  // AND_Gate and_5 has open pins: in0=B[3], in1=A[2], out=open
  // AND_Gate and_6 has open pins: in0=B[3], in1=A[1], out=open
  and and_7 (and_7_out, B[0], A[3]);
  and and_8 (and_8_out, B[1], A[2]);
  yet_another_full_adder yet_another_full_adder_3 (
    .A(and_7_out), .B(and_8_out), .Cin(yet_another_full_adder_4_cout), .Sum(yet_another_full_adder_3_sum),
    .Cout(yet_another_full_adder_3_cout));
  yet_another_full_adder yet_another_full_adder_4 (
    .A(and_11_out), .B(and_13_out), .Cin(half_adder_4_cout), .Sum(yet_another_full_adder_4_sum),
    .Cout(yet_another_full_adder_4_cout));
  and and_9 (and_9_out, B[2], A[1]);
  yet_another_full_adder yet_another_full_adder_5 (
    .A(yet_another_full_adder_3_sum), .B(and_9_out), .Cin(half_adder_3_cout),
    .Sum(yet_another_full_adder_5_sum), .Cout(yet_another_full_adder_5_cout));
  and and_10 (and_10_out, B[3], A[0]);
  half_adder half_adder_2 (.A(yet_another_full_adder_5_sum), .B(and_10_out), .SUM(res[3]));  // open: Cout
  and and_11 (and_11_out, B[0], A[2]);
  and and_12 (and_12_out, B[0], A[1]);
  and and_13 (and_13_out, B[1], A[1]);
  and and_14 (and_14_out, B[2], A[0]);
  half_adder half_adder_3 (.A(yet_another_full_adder_4_sum), .B(and_14_out), .Cout(half_adder_3_cout), .SUM(res[2]));
  and and_15 (res[0], B[0], A[0]);
  and and_16 (and_16_out, B[1], A[0]);
  half_adder half_adder_4 (.A(and_12_out), .B(and_16_out), .Cout(half_adder_4_cout), .SUM(res[1]));
endmodule

module yet_another_full_adder (
  input  A,
  input  B,
  input  Cin,
  output Sum,
  output Cout
);

  wire and_1_out, and_2_out, xor_1_out;

  xor xor_1 (xor_1_out, A, B);
  and and_1 (and_1_out, A, B);
  xor xor_2 (Sum, xor_1_out, Cin);
  and and_2 (and_2_out, xor_1_out, Cin);
  or or_1 (Cout, and_2_out, and_1_out);

  // Notes on the sheet:
  //   Ini biar tampilanny bisa beda aja
endmodule
